# Fritzing sketch Metronome (saved by Fritzing 0.9.4)
breadboards: 1

parts:
  U1 = ESP8266 NodeMCU LoLin module
  S2 = Pushbutton [package="[THT]"]
  Switch = SWITCH-MOMENTARY-2 [package=reed_switch_pth]
  Grove1 = Grove 4 Digit Display
  R1 = Resistor [tolerance=±5% resistance=220 package=THT]

nets:
  N1: U1.D1, U1.D3, S2.Pin_3, S2.Pin_4, Switch.2, R1.Pin_1
  GND: U1.GND, S2.Pin_1, S2.Pin_2, Switch.1, Grove1.GND
  N2: U1.D5, Grove1.DIO
  N3: U1.D6, Grove1.CLK
  VIN: U1.Vin, Grove1.VCC, R1.Pin_0

custom parts:
  ESP8266 NodeMCU LoLin module: ESP8266 based NodeMCU
